// Logisim project Limoncini_Matteo_910311_arch1lab_progetto.circ as structural Verilog: 15 circuits, main circuit Interfaccia Utente
module Interfaccia_Utente (
);

  wire button_1_out, button_2_out, button_3_out, button_4_out, button_5_out, button_6_out, button_7_out,
       button_8_out, button_9_out, button_10_out, r1, r2, r3, r4, r5, r6, r7, r8;
  wire [3:0] calcolo_punteggio_1_out, generatore_numero_1_out_2, generatore_numero_1_out_3, Numero;
  wire [4:0] dotmatrix_1_p1, dotmatrix_2_p1, dotmatrix_3_p1, dotmatrix_4_p1, dotmatrix_5_p1, dotmatrix_6_p1,
       dotmatrix_7_p1, dotmatrix_8_p1, row1, row2, row3, row4, row5, row6, row7, row8;
  wire [6:0] Col1, Col2, Col3, Col4, Col5, Col6, Col7, Col8, dotmatrix_1_p2, dotmatrix_2_p2, dotmatrix_3_p2,
       dotmatrix_4_p2, dotmatrix_5_p2, dotmatrix_6_p2, dotmatrix_7_p2, dotmatrix_8_p2;
  wire [7:0] Soluzioni;

  Hex_Digit_Display hex_digit_display_1 (.value(generatore_numero_1_out_2));  // open: dp
  Button button_1 (.out(button_1_out));
  Hex_Digit_Display hex_digit_display_2 (.value(generatore_numero_1_out_3));  // open: dp
  Generatore_Numero generatore_numero_1 (
    .out_4(Numero), .out_2(generatore_numero_1_out_2), .out_3(generatore_numero_1_out_3), .in_1(button_1_out));
  Button button_2 (.out(button_2_out));
  Button button_3 (.out(button_3_out));
  Button button_4 (.out(button_4_out));
  Button button_5 (.out(button_5_out));
  Button button_6 (.out(button_6_out));
  Button button_7 (.out(button_7_out));
  Button button_8 (.out(button_8_out));
  Button button_9 (.out(button_9_out));
  // DotMatrix #(.inputtype("select")) dotmatrix_1: pin names not known; wires that end beside it: dotmatrix_1_p1, dotmatrix_1_p2
  T_F_Display_Input t_f_display_input_1 (
    .out_2(dotmatrix_1_p1), .out_4(dotmatrix_1_p2), .out_3(r1), .in_1(button_2_out));
  // DotMatrix #(.inputtype("select")) dotmatrix_2: pin names not known; wires that end beside it: dotmatrix_2_p1, dotmatrix_2_p2
  T_F_Display_Input t_f_display_input_2 (
    .out_2(dotmatrix_2_p1), .out_4(dotmatrix_2_p2), .out_3(r2), .in_1(button_3_out));
  // DotMatrix #(.inputtype("select")) dotmatrix_3: pin names not known; wires that end beside it: dotmatrix_3_p1, dotmatrix_3_p2
  T_F_Display_Input t_f_display_input_3 (
    .out_2(dotmatrix_3_p1), .out_4(dotmatrix_3_p2), .out_3(r3), .in_1(button_4_out));
  // DotMatrix #(.inputtype("select")) dotmatrix_4: pin names not known; wires that end beside it: dotmatrix_4_p1, dotmatrix_4_p2
  T_F_Display_Input t_f_display_input_4 (
    .out_2(dotmatrix_4_p1), .out_4(dotmatrix_4_p2), .out_3(r4), .in_1(button_5_out));
  // DotMatrix #(.inputtype("select")) dotmatrix_5: pin names not known; wires that end beside it: dotmatrix_5_p1, dotmatrix_5_p2
  T_F_Display_Input t_f_display_input_5 (
    .out_2(dotmatrix_5_p1), .out_4(dotmatrix_5_p2), .out_3(r5), .in_1(button_6_out));
  // DotMatrix #(.inputtype("select")) dotmatrix_6: pin names not known; wires that end beside it: dotmatrix_6_p1, dotmatrix_6_p2
  T_F_Display_Input t_f_display_input_6 (
    .out_2(dotmatrix_6_p1), .out_4(dotmatrix_6_p2), .out_3(r6), .in_1(button_7_out));
  // DotMatrix #(.inputtype("select")) dotmatrix_7: pin names not known; wires that end beside it: dotmatrix_7_p1, dotmatrix_7_p2
  T_F_Display_Input t_f_display_input_7 (
    .out_2(dotmatrix_7_p1), .out_4(dotmatrix_7_p2), .out_3(r7), .in_1(button_8_out));
  // DotMatrix #(.inputtype("select")) dotmatrix_8: pin names not known; wires that end beside it: dotmatrix_8_p1, dotmatrix_8_p2
  T_F_Display_Input t_f_display_input_8 (
    .out_2(dotmatrix_8_p1), .out_4(dotmatrix_8_p2), .out_3(r8), .in_1(button_9_out));
  // DotMatrix #(.inputtype("select")) dotmatrix_9: pin names not known; wires that end beside it: row1, Col1
  // DotMatrix #(.inputtype("select")) dotmatrix_10: pin names not known; wires that end beside it: row2, Col2
  // DotMatrix #(.inputtype("select")) dotmatrix_11: pin names not known; wires that end beside it: row3, Col3
  // DotMatrix #(.inputtype("select")) dotmatrix_12: pin names not known; wires that end beside it: row4, Col4
  // DotMatrix #(.inputtype("select")) dotmatrix_13: pin names not known; wires that end beside it: row5, Col5
  // DotMatrix #(.inputtype("select")) dotmatrix_14: pin names not known; wires that end beside it: row6, Col6
  // DotMatrix #(.inputtype("select")) dotmatrix_15: pin names not known; wires that end beside it: row7, Col7
  // DotMatrix #(.inputtype("select")) dotmatrix_16: pin names not known; wires that end beside it: row8, Col8
  Hex_Digit_Display hex_digit_display_3 (.value(calcolo_punteggio_1_out));  // open: dp
  Calcolo_Punteggio calcolo_punteggio_1 (
    .in_1(r1), .in_2(r2), .in_3(r3), .utente(r4), .in_5(r5), .in_6(r6), .in_7(r7), .in_8(r8),
    .OUT(calcolo_punteggio_1_out), .in_9(Soluzioni));
  Button button_10 (.out(button_10_out));
  Correzioni_Output correzioni_output_1 (
    .in_1(Numero), .out_19(Soluzioni), .out_3(row1), .out_4(Col1), .out_5(row2), .out_6(Col2), .out_7(row3),
    .out_8(Col3), .out_9(row4), .out_10(Col4), .out_11(row5), .out_12(Col5), .out_13(row6), .out_14(Col6),
    .out_15(row7), .out_16(Col7), .out_17(row8), .out_18(Col8), .in_2(button_10_out));

  // Notes on the sheet:
  //   ^
  //   |
  //   Premi qui per
  //   cambiare numero
  //   è pari?
  //   è dispari?
  //   è primo?
  //   è perfetto?
  //   è divisibile per 3?
  //   è quadrato?
  //   è triangolare?
  //   è un primo
  //   di Mersenne?
  //   Rispondi alle domande,
  //   premi i pulsanti per selezionare
  //   vero (T) o falso (F) per la
  //   corrispondente domanda
  //   input
  //   utente
  //   risposta
  //   corretta
  //   ^
  //   |
  //   Premi qui per la correzione
  //   risposte giuste
  //   su 8 domande
endmodule

module Generatore_Numero (
  input  in_1,
  output [3:0] out_2,
  output [3:0] out_3,
  output [3:0] out_4
);

  wire _9, clock_1_out, comparator_1_lt, not_1_out;
  wire [3:0] controlled_buffer_1_out, counter_1_q, subtractor_1_out;

  Clock clock_1 (.out(clock_1_out));
  Comparator #(.width(4), .mode("unsigned")) comparator_1 (
    .a(out_4), .b(4'b1001), .gt(_9), .lt(comparator_1_lt));  // open: eq
  Random #(.width(4)) random_1 (.clk(clock_1_out), .next(in_1), .out(out_4));  // open: clr
  assign out_2 = {{3{1'b0}}, _9};  // Bit_Extender bit_extender_1
  assign controlled_buffer_1_out = comparator_1_lt ? out_4 : 4'bz;  // Controlled_Buffer controlled_buffer_1
  not not_1 (not_1_out, 1'b1);
  Counter #(.width(4), .max('h9)) counter_1 (
    .load(1'b1), .D(controlled_buffer_1_out), .count(not_1_out), .Q(counter_1_q), .clk(clock_1_out));  // open: carry, clr
  Multiplexer #(.width(4), .enable("false")) multiplexer_1 (
    .in0(counter_1_q), .in1(subtractor_1_out), .out(out_3), .sel(_9));
  Subtractor #(.width(4)) subtractor_1 (.a(out_4), .b(4'b1010), .out(subtractor_1_out));  // open: bin, bout
endmodule

module Correzioni (
  input  [3:0] numero,
  input  in_2,
  output out_3,
  output out_4,
  output out_5,
  output [7:0] soluzioni,
  output out_7,
  output out_8,
  output out_9,
  output out_10,
  output out_11
);

  wire t_ff_1_q;
  wire [3:0] controlled_buffer_1_out;

  assign controlled_buffer_1_out = t_ff_1_q ? numero : 4'bz;  // Controlled_Buffer controlled_buffer_1
  T_Flip_Flop t_ff_1 (.Q(t_ff_1_q), .preset(in_2));  // open: clk, T, Qn, reset, en
  Numeri_Perfetti numeri_perfetti_1 (.IN(controlled_buffer_1_out), .OUT(out_7));
  Numeri_Pari numeri_pari_1 (.IN(controlled_buffer_1_out), .OUT(out_3));
  Numeri_Dispari numeri_dispari_1 (.IN(controlled_buffer_1_out), .OUT(out_4));
  Numeri_Primi numeri_primi_1 (.IN(controlled_buffer_1_out), .OUT(out_5));
  Numeri_Divisibili_per_3 numeri_divisibili_per_3_1 (.IN(controlled_buffer_1_out), .OUT(out_8));
  Numeri_Quadrati numeri_quadrati_1 (.OUT(out_9), .IN(controlled_buffer_1_out));
  Numeri_Triangolari numeri_triangolari_1 (.OUT(out_10), .IN(controlled_buffer_1_out));
  Numeri_Primi_Mersenne numeri_primi_mersenne_1 (.IN(controlled_buffer_1_out), .OUT(out_11));

  assign soluzioni = {out_11, out_10, out_9, out_8, out_7, out_5, out_4, out_3};

  // Notes on the sheet:
  //   pulsante per la correzione
endmodule

module Correzioni_Output (
  input  [3:0] in_1,
  input  in_2,
  output [4:0] out_3,
  output [6:0] out_4,
  output [4:0] out_5,
  output [6:0] out_6,
  output [4:0] out_7,
  output [6:0] out_8,
  output [4:0] out_9,
  output [6:0] out_10,
  output [4:0] out_11,
  output [6:0] out_12,
  output [4:0] out_13,
  output [6:0] out_14,
  output [4:0] out_15,
  output [6:0] out_16,
  output [4:0] out_17,
  output [6:0] out_18,
  output [7:0] out_19
);

  wire correzioni_1_out_3, correzioni_1_out_4, correzioni_1_out_5, correzioni_1_out_7, correzioni_1_out_8,
       correzioni_1_out_9, correzioni_1_out_10, correzioni_1_out_11;

  Correzioni correzioni_1 (
    .numero(in_1), .in_2(in_2), .out_3(correzioni_1_out_3), .out_4(correzioni_1_out_4),
    .out_5(correzioni_1_out_5), .out_8(correzioni_1_out_8), .out_7(correzioni_1_out_7),
    .out_11(correzioni_1_out_11), .soluzioni(out_19), .out_10(correzioni_1_out_10), .out_9(correzioni_1_out_9));
  T_F_Display_Output t_f_display_output_1 (.in_1(correzioni_1_out_3), .righe(out_3), .out_3(out_4));
  T_F_Display_Output t_f_display_output_2 (.in_1(correzioni_1_out_4), .righe(out_5), .out_3(out_6));
  T_F_Display_Output t_f_display_output_3 (.in_1(correzioni_1_out_5), .righe(out_7), .out_3(out_8));
  T_F_Display_Output t_f_display_output_4 (.in_1(correzioni_1_out_7), .righe(out_9), .out_3(out_10));
  T_F_Display_Output t_f_display_output_5 (.in_1(correzioni_1_out_8), .righe(out_11), .out_3(out_12));
  T_F_Display_Output t_f_display_output_6 (.in_1(correzioni_1_out_10), .righe(out_13), .out_3(out_14));
  T_F_Display_Output t_f_display_output_7 (.in_1(correzioni_1_out_9), .righe(out_15), .out_3(out_16));
  T_F_Display_Output t_f_display_output_8 (.in_1(correzioni_1_out_11), .righe(out_17), .out_3(out_18));

  // Notes on the sheet:
  //   pulsante utente
  //   soluzioni
  //   righe e colonne display1
  //   righe e colonne display2
  //   righe e colonne display3
  //   righe e colonne display4
  //   righe e colonne display5
  //   righe e colonne display6
  //   righe e colonne display7
  //   righe e colonne display8
endmodule

module T_F_Display_Output (
  input  in_1,
  output [4:0] righe,
  output [6:0] out_3
);

  Multiplexer #(.width(5), .enable("false")) multiplexer_1 (.in0(5'b11110), .in1(5'b11011), .out(righe), .sel(in_1));
  Multiplexer #(.width(7), .enable("false")) multiplexer_2 (
    .in0(7'b0110111), .in1(7'b0111111), .out(out_3), .sel(in_1));

  // Notes on the sheet:
  //   colonne
endmodule

module T_F_Display_Input (
  input  in_1,
  output [4:0] out_2,
  output out_3,
  output [6:0] out_4
);

  wire d_ff_1_qn;

  D_Flip_Flop d_ff_1 (.clk(in_1), .D(d_ff_1_qn), .Q(out_3), .Qn(d_ff_1_qn));  // open: preset, en, reset
  Multiplexer #(.width(5), .enable("false")) multiplexer_1 (.in0(5'b11110), .in1(5'b11011), .out(out_2), .sel(out_3));
  Multiplexer #(.width(7), .enable("false")) multiplexer_2 (
    .in0(7'b0110111), .in1(7'b0111111), .out(out_4), .sel(out_3));
endmodule

module Calcolo_Punteggio (
  input  in_1,
  input  in_2,
  input  in_3,
  input  utente,
  input  in_5,
  input  in_6,
  input  in_7,
  input  in_8,
  input  [7:0] in_9,
  output [3:0] OUT
);

  wire xnor_1_out, xnor_2_out, xnor_3_out, xnor_4_out, xnor_5_out, xnor_6_out, xnor_7_out, xnor_8_out;

  xnor xnor_1 (xnor_1_out, in_1, in_9[0]);
  xnor xnor_2 (xnor_2_out, in_2, in_9[1]);
  xnor xnor_3 (xnor_3_out, in_3, in_9[2]);
  xnor xnor_4 (xnor_4_out, utente, in_9[3]);
  xnor xnor_5 (xnor_5_out, in_5, in_9[4]);
  xnor xnor_6 (xnor_6_out, in_6, in_9[5]);
  xnor xnor_7 (xnor_7_out, in_7, in_9[6]);
  xnor xnor_8 (xnor_8_out, in_8, in_9[7]);
  BitAdder #(.width(1)) bitadder_1 (
    .in0(xnor_1_out), .in1(xnor_2_out), .in2(xnor_3_out), .in3(xnor_4_out), .in4(xnor_5_out),
    .in5(xnor_6_out), .in6(xnor_7_out), .in7(xnor_8_out), .out(OUT));

  // Notes on the sheet:
  //   corretti
endmodule

module Numeri_Pari (
  input  [3:0] IN,
  output OUT
);

  not not_1 (OUT, IN[0]);

  // Notes on the sheet:
  //   (bit inutili)
  //   abcd
endmodule

module Numeri_Dispari (
  input  [3:0] IN,
  output OUT
);


  assign OUT = IN[0];

  // Notes on the sheet:
  //   (bit inutili)
  //   abcd
endmodule

module Numeri_Primi (
  input  [3:0] IN,
  output OUT
);

  wire and_1_out, and_2_out, and_3_out, and_4_out, xor_1_out;

  and and_1 (and_1_out, IN[1], ~IN[2], ~IN[3]);  // AND_Gate
  and and_2 (and_2_out, IN[0], IN[2], ~IN[3]);  // AND_Gate
  and and_3 (and_3_out, IN[0], IN[3]);
  xor xor_1 (xor_1_out, IN[1], IN[2]);
  and and_4 (and_4_out, and_3_out, xor_1_out);
  or or_1 (OUT, and_1_out, and_2_out, and_4_out);

  // Notes on the sheet:
  //   abcd
endmodule

module Numeri_Perfetti (
  input  [3:0] IN,
  output OUT
);

  and and_1 (OUT, ~IN[0], IN[1], IN[2], ~IN[3]);  // AND_Gate

  // Notes on the sheet:
  //   abcd
endmodule

module Numeri_Divisibili_per_3 (
  input  [3:0] IN,
  output OUT
);

  wire and_1_out, and_2_out, xor_1_out, xor_2_out;

  xor xor_1 (xor_1_out, IN[0], IN[2]);
  xor xor_2 (xor_2_out, IN[1], IN[3]);
  and and_1 (and_1_out, IN[0], IN[1], IN[2], IN[3]);
  and and_2 (and_2_out, xor_1_out, xor_2_out);
  or or_1 (OUT, and_1_out, and_2_out);

  // Notes on the sheet:
  //   abcd
endmodule

module Numeri_Quadrati (
  input  [3:0] IN,
  output OUT
);

  wire and_1_out, and_2_out, and_3_out, or_1_out;

  and and_1 (and_1_out, ~IN[1], ~IN[3]);  // AND_Gate
  or or_1 (or_1_out, ~IN[0], ~IN[2]);  // OR_Gate
  and and_2 (and_2_out, IN[0], ~IN[1], ~IN[2], IN[3]);  // AND_Gate
  and and_3 (and_3_out, and_1_out, or_1_out);
  or or_2 (OUT, and_3_out, and_2_out);

  // Notes on the sheet:
  //   abcd
endmodule

module Numeri_Triangolari (
  input  [3:0] IN,
  output OUT
);

  wire and_1_out, and_2_out, and_3_out, and_4_out, xnor_1_out;

  and and_1 (and_1_out, IN[0], ~IN[2], ~IN[3]);  // AND_Gate
  and and_2 (and_2_out, ~IN[0], IN[1], IN[2], ~IN[3]);  // AND_Gate
  and and_3 (and_3_out, IN[1], IN[3]);
  xnor xnor_1 (xnor_1_out, IN[0], IN[2]);
  and and_4 (and_4_out, and_3_out, xnor_1_out);
  or or_1 (OUT, and_1_out, and_2_out, and_4_out);

  // Notes on the sheet:
  //   abcd
endmodule

module Numeri_Primi_Mersenne (
  input  [3:0] IN,
  output OUT
);

  and and_1 (OUT, IN[0], IN[1], ~IN[3]);  // AND_Gate

  // Notes on the sheet:
  //   abcd
  //   (filo b inutile)
endmodule
